// Digital circuit instruction_mem.dig as structural Verilog
module instruction_mem (
  input  [31:0] address,
  output [31:0] instruction
);

  wire [31:0] div_1_q;

  Div #(.Bits(32)) div_1 (.a(address), .b(32'h4), .q(div_1_q));  // open: r
  ROM #(.AddrBits(8), .Bits(32)) rom_1 (.A(div_1_q[7:0]), .sel(1'b1), .D(instruction));

  // Notes on the sheet:
  //   contents of rom_1 (hex, n*v repeats v):
  //   20090000,200a0001,201f0001,12a6020,a4820,c5020,cf820,8000003
endmodule
