// Digital circuit memory_24x32.dig as structural Verilog
module memory_24x32 (
  input  [23:0] A,
  input  [31:0] Data_in,
  input  MW,
  input  Clk,
  input  MR,
  output [31:0] D
);

  RAMDualPort #(.AddrBits(24), .Bits(32)) ramdualport_1 (.A(A), .Din(Data_in), .str(MW), .C(Clk), .ld(MR), .D(D));

  // Notes on the sheet:
  //   A: Endereço a ser acessado
  //   Data_in: Dados a serem gravados
  //   MW: Mem Write
  //   Clk: Clock
  //   MR: Mem Read
  //   D: Saída da memória
endmodule
