// Digital circuit Stall.dig as structural Verilog
module Stall (
  input  ID_EX_memRead,
  input  [4:0] ID_EX_rt,
  input  [4:0] IF_ID_rs,
  input  [4:0] IF_ID_rt,
  output Stall
);

  wire comparator_1_eq, comparator_2_eq, or_1_out;

  and and_1 (Stall, ID_EX_memRead, or_1_out);
  or or_1 (or_1_out, comparator_2_eq, comparator_1_eq);
  Comparator #(.Bits(5)) comparator_1 (.a(IF_ID_rs), .b(ID_EX_rt), .eq(comparator_1_eq));  // open: gt, lt
  Comparator #(.Bits(5)) comparator_2 (.a(IF_ID_rt), .b(ID_EX_rt), .eq(comparator_2_eq));  // open: gt, lt
endmodule
