// Digital circuit main.dig as structural Verilog
module main (
  input  clock,
  input  pc_reset
);

  wire ALU_Control_p2, ALU_Control_p5, and_1_out, APC, Banco_de_registradores_p1, Banco_de_registradores_p7,
       Banco_de_registradores_p8, ex_mem_1_mem_memread, ex_mem_1_mem_memtoreg, ex_mem_1_mem_memwrite,
       ex_mem_1_wb_regwrite, ex_mem_pc_1_o_apc, ex_mem_pc_1_o_zero, id_ex_1_p16, id_ex_1_p17, id_ex_1_p18,
       id_ex_1_p19, id_ex_1_p20, id_ex_1_p21, id_ex_1_p22, id_ex_pc_1_o_apc, if_id_1_p2,
       mem_wb_1_wb_memtoreg, stall_1_stall, ULA_p5;
  wire [1:0] FA, FB;
  wire [4:0] ALU_Control_p1, Banco_de_registradores_p5, ex_mem_1_mem_dstaddr, multiplexer_3_out, undriven_2,
       undriven_3;
  wire [5:0] if_id_1_p6, if_id_1_p6_3;
  wire [7:0] multiplexer_2_out, UC_mw;
  wire [25:6] if_id_1_p6_2;
  wire [31:0] add_1_s, barrelshifter_1_out, bitextender_1_out, ex_mem_1_mem_rtdata, ex_mem_pc_1_o_pc,
       id_ex_1_p23, id_ex_1_p24, id_ex_pc_1_o_pc, Mem_result, mem_wb_1_wb_readdata, mem_wb_1_wb_result,
       \Memória_de_dados_data , multiplexer_1_out, multiplexer_4_out, multiplexer_5_out, multiplexer_6_out,
       pc_1_address, pc_ppl_1_o_pc, R31, ULA_p6, undriven, WB;

  Multiplexer #(.Bits(32)) multiplexer_1 (
    .sel(and_1_out), .in_0(add_1_s), .in_1(ex_mem_pc_1_o_pc), .out(multiplexer_1_out));
  Seven_Seg_Hex seven_seg_hex_1 (.d(R31[19:16]), .dp(1'b0));
  Seven_Seg_Hex seven_seg_hex_2 (.d(R31[15:12]), .dp(1'b0));
  PC pc_1 (.clock(clock), .write(multiplexer_1_out), .reset(pc_reset), .address(pc_1_address));
  Seven_Seg_Hex seven_seg_hex_3 (.d(R31[11:8]), .dp(1'b0));
  Seven_Seg_Hex seven_seg_hex_4 (.d(R31[7:4]), .dp(1'b0));
  Add #(.Bits(32)) add_1 (.a(pc_1_address), .b(32'h4), .c_i(1'b0), .s(add_1_s));  // open: c_o
  Seven_Seg_Hex seven_seg_hex_5 (.d(R31[3:0]), .dp(1'b0));
  instruction_mem \Memória_de_instruções  ();  // open: _32b__ADDR, _1b__Enable, _32b__Out
  // IF_ID if_id_1: pin names not known; wires that end beside it: pc_1_address, if_id_1_p2, if_id_1_p2, 1'b1, clock, {if_id_1_p6_3, if_id_1_p6_2, if_id_1_p6}
  PC_ppl pc_ppl_1 (.PC(add_1_s), .Clk(clock), .O_PC(pc_ppl_1_o_pc));
  Control UC (
    .RgD(UC_mw[0]), .AluS(UC_mw[1]), .MTR(UC_mw[2]), .RW(UC_mw[3]), .MR(UC_mw[4]), .MW(UC_mw[5]),
    .AO_1(UC_mw[6]), .AO_0(UC_mw[7]), .APC(APC), .Op(if_id_1_p6_3), .Clk(clock));  // open: B, J
  // _32x32 Banco_de_registradores: pin names not known; wires that end beside it: Banco_de_registradores_p1, WB, if_id_1_p6_2[25:21], if_id_1_p6_2[20:16], Banco_de_registradores_p5, clock, Banco_de_registradores_p7, Banco_de_registradores_p8, R31
  BitExtender #(.inputBits(16), .outputBits(32)) bitextender_1 (
    .in({if_id_1_p6_2[15:6], if_id_1_p6}), .out(bitextender_1_out));
  Multiplexer #(.Bits(8)) multiplexer_2 (.sel(stall_1_stall), .in_0(UC_mw), .in_1({8{1'b0}}), .out(multiplexer_2_out));
  Stall stall_1 (
    .IF_ID_rs(if_id_1_p6_2[25:21]), .IF_ID_rt(if_id_1_p6_2[20:16]), .ID_EX_memRead(id_ex_1_p18),
    .ID_EX_rt(undriven_3), .Stall(stall_1_stall));
  // ID_EX id_ex_1: pin names not known; wires that end beside it: multiplexer_2_out[3], multiplexer_2_out[2], multiplexer_2_out[4], multiplexer_2_out[5], multiplexer_2_out[0], multiplexer_2_out[1], multiplexer_2_out[7:6], Banco_de_registradores_p7, Banco_de_registradores_p8, bitextender_1_out, if_id_1_p6_2[25:21], if_id_1_p6_2[20:16], if_id_1_p6_2[15:11], if_id_1_p6, clock, id_ex_1_p16, id_ex_1_p17, id_ex_1_p18, id_ex_1_p19, id_ex_1_p20, id_ex_1_p21, id_ex_1_p22, id_ex_1_p23, id_ex_1_p24
  ID_EX_PC id_ex_pc_1 (.PC(pc_ppl_1_o_pc), .APC(APC), .Clk(clock), .O_PC(id_ex_pc_1_o_pc), .O_APC(id_ex_pc_1_o_apc));
  BarrelShifter #(.Bits(32)) barrelshifter_1 (.in(undriven), .shift(6'b000010), .out(barrelshifter_1_out));
  Multiplexer #(.Bits(5)) multiplexer_3 (
    .sel(id_ex_1_p20), .in_0(undriven_3), .in_1(ALU_Control_p1), .out(multiplexer_3_out));
  Multiplexer #(.Selector_Bits(2), .Bits(32)) multiplexer_4 (
    .sel(FB), .in_0(id_ex_1_p24), .in_1(WB), .in_2(Mem_result), .in_3(Mem_result), .out(multiplexer_4_out));
  // ALU_Control ALU_Control: pin names not known; wires that end beside it: ALU_Control_p1, ALU_Control_p2, id_ex_1_p22, ALU_Control_p2, ALU_Control_p5
  Add #(.Bits(32)) add_2 (.a(id_ex_pc_1_o_pc), .b(barrelshifter_1_out), .c_i(1'b0));  // open: s, c_o
  Multiplexer #(.Bits(32)) multiplexer_5 (
    .sel(id_ex_1_p21), .in_0(multiplexer_4_out), .in_1(undriven), .out(multiplexer_5_out));
  Multiplexer #(.Selector_Bits(2), .Bits(32)) multiplexer_6 (
    .sel(FA), .in_0(id_ex_1_p23), .in_1(WB), .in_2(Mem_result), .in_3(Mem_result), .out(multiplexer_6_out));
  // ula ULA: pin names not known; wires that end beside it: ALU_Control_p5, multiplexer_6_out, multiplexer_5_out, {6{1'b0}}, ULA_p5, ULA_p6
  forwarding_unit Unidade_de_forwarding (
    .RS(undriven_2), .RT(undriven_3), .EX_MEM_dest(ex_mem_1_mem_dstaddr),
    .MEM_WB_dest(Banco_de_registradores_p5), .EX_MEM_rw(ex_mem_1_wb_regwrite),
    .MEM_WB_rw(Banco_de_registradores_p1), .FA(FA), .FB(FB));
  EX_MEM_PC ex_mem_pc_1 (
    .PC(barrelshifter_1_out), .Alu_zero(ULA_p5), .APC(id_ex_pc_1_o_apc), .Clk(clock),
    .O_PC(ex_mem_pc_1_o_pc), .O_zero(ex_mem_pc_1_o_zero), .O_APC(ex_mem_pc_1_o_apc));
  EX_MEM ex_mem_1 (
    .EX_regWrite(id_ex_1_p16), .EX_memRead(id_ex_1_p18), .EX_memWrite(id_ex_1_p19),
    .EX_memToReg(id_ex_1_p17), .EX_result(ULA_p6), .EX_rtData(multiplexer_4_out),
    .EX_dstAddr(multiplexer_3_out), .clock(clock), .WB_regWrite(ex_mem_1_wb_regwrite),
    .MEM_memRead(ex_mem_1_mem_memread), .MEM_memWrite(ex_mem_1_mem_memwrite),
    .MEM_memToReg(ex_mem_1_mem_memtoreg), .MEM_result(Mem_result), .MEM_rtData(ex_mem_1_mem_rtdata),
    .MEM_dstAddr(ex_mem_1_mem_dstaddr));
  and and_1 (and_1_out, ex_mem_pc_1_o_zero, ~ex_mem_pc_1_o_apc);  // And
  memory_24x32 \Memória_de_dados  (
    .address(Mem_result[23:0]), .write_data(ex_mem_1_mem_rtdata), .mem_write(ex_mem_1_mem_memwrite),
    .mem_read(ex_mem_1_mem_memread), .clock(clock), .data(\Memória_de_dados_data ));
  MEM_WB mem_wb_1 (
    .MEM_regWrite(ex_mem_1_wb_regwrite), .MEM_memToReg(ex_mem_1_mem_memtoreg),
    .MEM_readData(\Memória_de_dados_data ), .MEM_result(Mem_result), .MEM_dstAddr(ex_mem_1_mem_dstaddr),
    .clock(clock), .WB_regWrite(Banco_de_registradores_p1), .WB_memToReg(mem_wb_1_wb_memtoreg),
    .WB_readData(mem_wb_1_wb_readdata), .WB_result(mem_wb_1_wb_result), .WB_dstAddr(Banco_de_registradores_p5));
  Multiplexer #(.Bits(32)) multiplexer_7 (
    .sel(mem_wb_1_wb_memtoreg), .in_0(mem_wb_1_wb_result), .in_1(mem_wb_1_wb_readdata), .out(WB));

  // Notes on the sheet:
  //   clock: Hz: 10
  //   Instruções na memória
  //   loop:
  //   addi $ra, $ra 1
  //   j loop
  //   001000 11111 11111 00000 00000000001
  //   000010 00000 00000 00000 00000000000
  //   23ff0001
  //   08000000
  //   Não adiciona o valor ao PC
  //   Reg Destino
  //   MEM/WB_Dest
  //   MEM/WB_RegWrite
endmodule
